# Fritzing sketch Rangkaian (saved by Fritzing 0.9.3b)

parts:
  Part1 = Arduino Ethernet Shield (Rev3)
  Part2 = Arduino Uno (Rev3) - ICSP  # not connected
  S1 = 5-channel flame detector module
  Part3 = MQ-3 breakout
  Part4 = IFR520 MOS module [package=THT]
  J1 = Piezo Speaker
  JACK1 = 2.1mm Barrel Jack with Terminal Block

nets:
  N1: Part1.D8, S1.pin11
  N2: Part1.PWM_D9, S1.pin13
  N3: Part1.A0, Part3.AO
  N4: Part1.D2, Part4.pin1
  N5: Part1.PWM_D5, S1.pin5
  N6: Part1.PWM_D6, S1.pin7
  N7: Part1.D7, S1.pin9
  N8: Part1.3V3, Part4.pin2
  5V: Part1.5V, S1.pin3, S1.pin4, Part3.VCC
  GND: Part1.GND, S1.pin1, S1.pin2, Part3.GND, Part4.pin3
  N9: Part4.pin4, J1.pin2
  N10: Part4.pin5, J1.pin1
  N11: Part4.pin6, JACK1.POS
  N12: Part4.pin7, JACK1.NEG

custom parts:
  MQ-3 breakout: Alcohol sensor is capable of detecting alcohol (ethanol) particles on itself and gives the information in digital form back to us to manipulate with it. SKU:101251 • Voltage: 5V DC • Power: max 750mW • Measurement range: 0.04-4mg/L
